// Logisim project projeto_circuito_2 (1).circ as structural Verilog: 10 circuits, main circuit main
module main (
  input  in_1
);

  wire A, ALARM, ALTER, button_5_out, C, H, M, MODE, N, PAUSE, RESET, RST_A, S, SELECT;
  wire [3:0] DH, DM, DS, UH, UM, US;

  Button button_1 (.out(SELECT));
  Button button_2 (.out(PAUSE));
  LED led_1 (.in(H));
  Hex_Digit_Display hex_digit_display_1 (.value(UH));  // open: dp
  Hex_Digit_Display hex_digit_display_2 (.value(DH));  // open: dp
  LED led_2 (.in(C));
  Hex_Digit_Display hex_digit_display_3 (.value(DM));  // open: dp
  LED led_3 (.in(M));
  Hex_Digit_Display hex_digit_display_4 (.value(UM));  // open: dp
  LED led_4 (.in(A));
  LED led_5 (.in(ALARM));
  Hex_Digit_Display hex_digit_display_5 (.value(DS));  // open: dp
  LED led_6 (.in(S));
  Hex_Digit_Display hex_digit_display_6 (.value(US));  // open: dp
  LED led_7 (.in(N));
  demu demu_1 (
    .C(C), .H(H), .M(M), .S(S), .A(A), .N(N), .US(US), .DS(DS), .UM(UM), .DM(DM), .SELECT_minus(SELECT),
    .ALARM_minus(ALARM), .UH(UH), .DH(DH), .PAUSE_minus(PAUSE), .in_6(in_1), .MODE_minus(MODE),
    .ALTER_minus(ALTER), .RESET_minus(RESET), .RST_A(RST_A));  // open: ALARM_2
  Button button_3 (.out(MODE));
  Button button_4 (.out(ALTER));
  Button button_5 (.out(button_5_out));
  Button button_6 (.out(RESET));
  Button button_7 (.out(RST_A));
endmodule

module cont_09 (
  input  clk,
  input  rst,
  output [3:0] display,
  output next
);

  wire or_1_out;
  wire [3:0] adder_1_out;

  Hex_Digit_Display hex_digit_display_1 (.value(display));  // open: dp
  Register #(.width(4)) register_1 (.D(adder_1_out), .Q(display), .clk(clk), .clr(or_1_out));  // open: en
  or or_1 (or_1_out, next, rst);
  Adder #(.width(4)) adder_1 (.a(display), .b(4'b0001), .out(adder_1_out));  // open: cin, cout
  and and_1 (next, display[3], ~display[2], display[1], ~display[0]);  // AND_Gate
endmodule

module cont_059 (
  input  clk_seg,
  input  reset,
  output [3:0] dezena,
  output [3:0] unidade,
  output next
);

  wire cont_09_2_next, or_1_out;

  and and_1 (next, ~dezena[0], dezena[1], dezena[2], ~dezena[3]);  // AND_Gate
  or or_1 (or_1_out, next, reset);
  Hex_Digit_Display hex_digit_display_1 (.value(dezena));  // open: dp
  cont_09 cont_09_1 (.display(dezena), .clk(cont_09_2_next), .rst(or_1_out));  // open: next
  Hex_Digit_Display hex_digit_display_2 (.value(unidade));  // open: dp
  cont_09 cont_09_2 (.display(unidade), .clk(clk_seg), .rst(or_1_out), .next(cont_09_2_next));
endmodule

module cont_min (
  input  clk_min,
  input  reset,
  output [3:0] dezena,
  output [3:0] unidade,
  output next
);

  wire cont_09_2_next, or_1_out;
  wire [3:0] undriven, undriven_2;

  and and_1 (next, ~dezena[0], dezena[1], dezena[2], ~dezena[3]);  // AND_Gate
  or or_1 (or_1_out, next, reset);
  Hex_Digit_Display hex_digit_display_1 (.value(dezena));  // open: dp
  cont_09 cont_09_1 (.display(dezena), .clk(cont_09_2_next), .rst(or_1_out));  // open: next
  Hex_Digit_Display hex_digit_display_2 (.value(unidade));  // open: dp
  cont_09 cont_09_2 (.display(unidade), .clk(clk_min), .rst(or_1_out), .next(cont_09_2_next));
  Hex_Digit_Display hex_digit_display_3 (.value(undriven));  // open: dp
  Hex_Digit_Display hex_digit_display_4 (.value(undriven_2));  // open: dp
endmodule

module cont_hr (
  input  clk_hr,
  input  reset_hr,
  output [3:0] dez_hr,
  output [3:0] uni_hr
);

  wire and_1_out, and_2_out, and_3_out, cont_09_2_next, or_1_out;

  and and_1 (and_1_out, ~dez_hr[0], dez_hr[1], ~dez_hr[2], ~dez_hr[3]);  // AND_Gate
  Hex_Digit_Display hex_digit_display_1 (.value(dez_hr));  // open: dp
  Hex_Digit_Display hex_digit_display_2 (.value(uni_hr));  // open: dp
  cont_09 cont_09_1 (.display(dez_hr), .clk(cont_09_2_next), .rst(or_1_out));  // open: next
  or or_1 (or_1_out, reset_hr, and_2_out);
  and and_2 (and_2_out, and_1_out, and_3_out);
  cont_09 cont_09_2 (.display(uni_hr), .clk(clk_hr), .rst(or_1_out), .next(cont_09_2_next));
  and and_3 (and_3_out, ~uni_hr[3], uni_hr[2], ~uni_hr[1], ~uni_hr[0]);  // AND_Gate
endmodule

module teste (
  input  CLK,
  input  HORA_R,
  input  MIN_R,
  input  ON_OFF,
  input  SEG_R,
  input  rst,
  output [3:0] min_dez,
  output [3:0] seg_dez,
  output [3:0] seg_uni,
  output [3:0] hr_dez,
  output [3:0] hr_uni,
  output [3:0] min_uni
);

  wire and_1_out, cont_059_1_next, cont_min_1_next, or_1_out, or_2_out, or_3_out;

  Hex_Digit_Display hex_digit_display_1 (.value(hr_dez));  // open: dp
  cont_hr cont_hr_1 (.dez_hr(hr_dez), .reset_hr(rst), .uni_hr(hr_uni), .clk_hr(or_1_out));
  Hex_Digit_Display hex_digit_display_2 (.value(hr_uni));  // open: dp
  or or_1 (or_1_out, cont_min_1_next, HORA_R);
  Hex_Digit_Display hex_digit_display_3 (.value(min_dez));  // open: dp
  Hex_Digit_Display hex_digit_display_4 (.value(min_uni));  // open: dp
  cont_min cont_min_1 (.dezena(min_dez), .unidade(min_uni), .next(cont_min_1_next), .reset(rst), .clk_min(or_2_out));
  or or_2 (or_2_out, cont_059_1_next, MIN_R);
  Hex_Digit_Display hex_digit_display_5 (.value(seg_dez));  // open: dp
  Hex_Digit_Display hex_digit_display_6 (.value(seg_uni));  // open: dp
  cont_059 cont_059_1 (.dezena(seg_dez), .next(cont_059_1_next), .reset(rst), .unidade(seg_uni), .clk_seg(or_3_out));
  or or_3 (or_3_out, and_1_out, SEG_R);
  and and_1 (and_1_out, CLK, ON_OFF);
endmodule

module comp (
  input  [3:0] UNID_SEG_HR,
  input  [3:0] UNID_SEG_AL,
  input  [3:0] DEZ_SEG_HR,
  input  [3:0] DEZ_SEG_AL,
  input  [3:0] UNID_MIN_HR,
  input  [3:0] UNID_MIN_AL,
  input  [3:0] DEZ_MIN_HR,
  input  [3:0] DEZ_MIN_AL,
  input  [3:0] UNID_HR_R,
  input  [3:0] UNID_HR_AL,
  input  [3:0] DEZ_HR_R,
  input  [3:0] UNID_HR_AL_2,
  output LED
);

  wire comparator_1_eq, comparator_2_eq, comparator_3_eq, comparator_4_eq, comparator_5_eq, comparator_6_eq;

  Comparator #(.width(4)) comparator_1 (.a(UNID_SEG_HR), .b(UNID_SEG_AL), .eq(comparator_1_eq));  // open: gt, lt
  Comparator #(.width(4)) comparator_2 (.a(DEZ_SEG_HR), .b(DEZ_SEG_AL), .eq(comparator_2_eq));  // open: gt, lt
  Comparator #(.width(4)) comparator_3 (.a(UNID_MIN_HR), .b(UNID_MIN_AL), .eq(comparator_3_eq));  // open: gt, lt
  Comparator #(.width(4)) comparator_4 (.a(DEZ_MIN_HR), .b(DEZ_MIN_AL), .eq(comparator_4_eq));  // open: gt, lt
  Comparator #(.width(4)) comparator_5 (.a(UNID_HR_R), .b(UNID_HR_AL), .eq(comparator_5_eq));  // open: gt, lt
  Comparator #(.width(4)) comparator_6 (.a(DEZ_HR_R), .b(UNID_HR_AL_2), .eq(comparator_6_eq));  // open: gt, lt
  and and_1 (LED, comparator_1_eq, comparator_2_eq, comparator_3_eq, comparator_4_eq, comparator_5_eq, comparator_6_eq);
endmodule

module multiplex (
  input  ON_OFF,
  input  CHANGE,
  input  [3:0] DHR,
  input  [3:0] DHA,
  input  [3:0] UHR,
  input  [3:0] UHA,
  input  [3:0] DMR,
  input  [3:0] DMA,
  input  [3:0] UMR,
  input  [3:0] UMA,
  input  [3:0] DSR,
  input  [3:0] DSA,
  input  [3:0] USR,
  input  [3:0] USA,
  output [3:0] DH,
  output [3:0] UH,
  output [3:0] DM,
  output [3:0] UM,
  output [3:0] DS,
  output [3:0] US
);

  wire button_1_out, undriven, undriven_2, undriven_3;
  wire [1:0] counter_1_q;

  Multiplexer #(.width(4)) multiplexer_1 (.in0(DHR), .in1(DHA), .out(DH), .sel(CHANGE), .en(ON_OFF));
  Multiplexer #(.width(4)) multiplexer_2 (.in0(UHR), .in1(UHA), .out(UH), .sel(CHANGE), .en(ON_OFF));
  Multiplexer #(.width(4)) multiplexer_3 (.in0(DMR), .in1(DMA), .out(DM), .sel(CHANGE), .en(ON_OFF));
  Counter #(.width(2), .max('h3)) counter_1 (.Q(counter_1_q), .clk(button_1_out));  // open: load, D, count, carry, clr
  Button button_1 (.out(button_1_out));
  Multiplexer #(.width(4)) multiplexer_4 (.in0(UMR), .in1(UMA), .out(UM), .sel(CHANGE), .en(ON_OFF));
  Multiplexer #(.width(4)) multiplexer_5 (.in0(DSR), .in1(DSA), .out(DS), .sel(CHANGE), .en(ON_OFF));
  Multiplexer #(.width(4)) multiplexer_6 (.in0(USR), .in1(USA), .out(US), .sel(CHANGE), .en(ON_OFF));
  Multiplexer #(.select(2), .enable("false")) multiplexer_7 (
    .in0(undriven), .in2(undriven_2), .in3(undriven_3), .sel(counter_1_q));  // open: in1, out

  // Other names for the same wires on the sheet: Al_Rel = CHANGE; LIGAR = ON_OFF
endmodule

module ALTERADOR (
  input  ENTRADA,
  output [1:0] MS,
  output MIN,
  output SEG,
  output HR
);

  wire and_1_out, and_2_out, nor_1_out;
  wire [1:0] adder_1_out;

  Counter #(.width(2), .max('h3)) counter_1 (
    .D(adder_1_out), .Q({HR, MIN}), .clk(ENTRADA));  // open: load, count, carry, clr
  Adder #(.width(2)) adder_1 (.a({HR, MIN}), .b(2'b11), .out(adder_1_out));  // open: cin, cout
  LED led_1 (.in(MIN));
  LED led_2 (.in(HR));
  and and_1 (and_1_out, MIN, HR);
  nor nor_1 (nor_1_out, MIN, HR);
  LED led_3 (.in(SEG));
  or or_1 (SEG, and_1_out, nor_1_out);
  and and_2 (and_2_out, SEG, MIN, HR);
  LED led_4 (.in(and_2_out));

  assign MS = {HR, MIN};

  // Other names for the same wires on the sheet: M = MIN; H = HR; S = SEG
endmodule

module demu (
  input  SELECT_minus,
  input  MODE_minus,
  input  ALTER_minus,
  input  RST_A,
  input  RESET_minus,
  input  in_6,
  input  PAUSE_minus,
  input  ALARM_2,
  output H,
  output M,
  output S,
  output A,
  output C,
  output [3:0] US,
  output [3:0] UH,
  output N,
  output [3:0] DS,
  output [3:0] DH,
  output [3:0] UM,
  output [3:0] DM,
  output ALARM_minus
);

  wire A_t, B, CLK, comp_1_led, counter_1_q, demultiplexer_1_out3, demultiplexer_2_out3,
       demultiplexer_3_out0, HORA_A, HORA_R, MIN_A, MIN_R, SEG_A, SEG_R;
  wire [1:0] alterador_1_ms;
  wire [3:0] DHA, DHR, DMA, DMR, DSA, DSR, UHA, UHR, UMA, UMR, USA, USR;

  Hex_Digit_Display hex_digit_display_1 (.value(DHR));  // open: dp
  Hex_Digit_Display hex_digit_display_2 (.value(UHR));  // open: dp
  ALTERADOR alterador_1 (.MS(alterador_1_ms), .MIN(M), .ENTRADA(SELECT_minus), .HR(H), .SEG(S));
  Demultiplexer #(.select(2), .enable("false")) demultiplexer_1 (
    .out0(SEG_R), .out1(MIN_R), .out2(HORA_R), .out3(demultiplexer_1_out3), .in(A_t), .sel(alterador_1_ms));
  Hex_Digit_Display hex_digit_display_3 (.value(DMR));  // open: dp
  Hex_Digit_Display hex_digit_display_4 (.value(UMR));  // open: dp
  comp comp_1 (
    .UNID_SEG_HR(USR), .UNID_SEG_AL(USA), .DEZ_SEG_HR(DSR), .DEZ_SEG_AL(DSA), .UNID_MIN_HR(UMR),
    .UNID_MIN_AL(UMA), .DEZ_MIN_HR(DMR), .DEZ_MIN_AL(DMA), .UNID_HR_R(UHR), .UNID_HR_AL(UHA), .DEZ_HR_R(DHR),
    .UNID_HR_AL_2(DHA), .LED(comp_1_led));
  Register #(.width(1)) register_1 (.D(comp_1_led), .en(comp_1_led), .Q(ALARM_minus), .clk(CLK), .clr(ALARM_2));
  Hex_Digit_Display hex_digit_display_5 (.value(DSR));  // open: dp
  Clock clock_1 (.out(CLK));
  LED led_1 (.in(H));
  Hex_Digit_Display hex_digit_display_6 (.value(DH));  // open: dp
  Hex_Digit_Display hex_digit_display_7 (.value(USR));  // open: dp
  Counter #(.width(1), .max('h1)) counter_1 (.Q(counter_1_q), .clk(PAUSE_minus));  // open: load, D, count, carry, clr
  Hex_Digit_Display hex_digit_display_8 (.value(UH));  // open: dp
  teste teste_1 (
    .min_dez(DMR), .hr_dez(DHR), .hr_uni(UHR), .rst(RESET_minus), .min_uni(UMR), .seg_dez(DSR),
    .seg_uni(USR), .HORA_R(HORA_R), .ON_OFF(counter_1_q), .MIN_R(MIN_R), .SEG_R(SEG_R), .CLK(CLK));
  LED led_2 (.in(M));
  Hex_Digit_Display hex_digit_display_9 (.value(DM));  // open: dp
  Hex_Digit_Display hex_digit_display_10 (.value(UM));  // open: dp
  Demultiplexer #(.select(2), .enable("false")) demultiplexer_2 (
    .out0(SEG_A), .out1(MIN_A), .out2(HORA_A), .out3(demultiplexer_2_out3), .in(B), .sel(alterador_1_ms));
  LED led_3 (.in(S));
  Hex_Digit_Display hex_digit_display_11 (.value(DS));  // open: dp
  Hex_Digit_Display hex_digit_display_12 (.value(US));  // open: dp
  Hex_Digit_Display hex_digit_display_13 (.value(UHA));  // open: dp
  Hex_Digit_Display hex_digit_display_14 (.value(DHA));  // open: dp
  Counter #(.width(2), .max('h2)) counter_2 (.Q({C, A}), .clk(MODE_minus));  // open: load, D, count, carry, clr
  Hex_Digit_Display hex_digit_display_15 (.value(DMA));  // open: dp
  // teste teste_2: pin names not known; wires that end beside it: DHA, UHA, CLK, in_6, DMA, HORA_A, MIN_A, UMA, SEG_A, RST_A, DSA, USA
  Demultiplexer #(.select(2), .enable("false")) demultiplexer_3 (
    .out0(demultiplexer_3_out0), .out1(B), .out2(A_t), .in(ALTER_minus), .sel({C, A}));  // open: out3
  Hex_Digit_Display hex_digit_display_16 (.value(UMA));  // open: dp
  Hex_Digit_Display hex_digit_display_17 (.value(DSA));  // open: dp
  Hex_Digit_Display hex_digit_display_18 (.value(USA));  // open: dp
  multiplex multiplex_1 (
    .DH(DH), .UH(UH), .DM(DM), .UM(UM), .DS(DS), .US(US), .ON_OFF(1'b1), .CHANGE(A), .DHR(DHR), .DHA(DHA),
    .UHR(UHR), .UHA(UHA), .DMR(DMR), .DMA(DMA), .UMR(UMR), .UMA(UMA), .DSR(DSR), .DSA(DSA), .USR(USR),
    .USA(USA));
  LED led_4 (.in(C));
  LED led_5 (.in(A));
  nor nor_1 (N, C, A);
  LED led_6 (.in(N));

  // Other names for the same wires on the sheet: ON_OFF = in_6; RST = RESET_minus; S_t[1:0] = {C, A}
endmodule
