// Logisim project projeto_circuito_2.circ as structural Verilog: 10 circuits, main circuit main
module main (
  input  in_1,
  input  in_2,
  input  in_3,
  input  in_4,
  input  in_5,
  input  in_6,
  output out_7,
  output out_8,
  output [1:0] out_9
);

  wire alterador_1_hr, alterador_1_min, alterador_1_seg, button_1_out, button_2_out, button_4_out,
       clock_1_out, comp_1_led, demultiplexer_1_out3, demultiplexer_2_out3, HORA_A, HORA_R, MIN_A, MIN_R,
       RST, RST_A;
  wire [3:0] DH, DHA, DHR, DM, DMA, DMR, DS, DSA, DSR, UH, UHA, UHR, UM, UMA, UMR, US, USA, USR;

  Hex_Digit_Display hex_digit_display_1 (.value(DHR));  // open: dp
  Button button_1 (.out(button_1_out));
  Hex_Digit_Display hex_digit_display_2 (.value(UHR));  // open: dp
  ALTERADOR alterador_1 (
    .MS(out_9), .MIN(alterador_1_min), .ENTRADA(button_1_out), .HR(alterador_1_hr), .SEG(alterador_1_seg));
  Demultiplexer #(.select(2), .enable("false")) demultiplexer_1 (
    .out0(out_7), .out1(MIN_R), .out2(HORA_R), .out3(demultiplexer_1_out3), .in(button_2_out), .sel(out_9));
  Button button_2 (.out(button_2_out));
  Hex_Digit_Display hex_digit_display_3 (.value(UMR));  // open: dp
  Hex_Digit_Display hex_digit_display_4 (.value(DMR));  // open: dp
  comp comp_1 (
    .UNID_SEG_HR(USR), .UNID_SEG_AL(USA), .DEZ_SEG_HR(DSR), .DEZ_SEG_AL(DSA), .UNID_MIN_HR(UMR),
    .UNID_MIN_AL(UMA), .DEZ_MIN_HR(DMR), .DEZ_MIN_AL(DMA), .UNID_HR_R(UHR), .UNID_HR_AL(UHA), .DEZ_HR_R(DHR),
    .UNID_HR_AL_2(DHA), .LED(comp_1_led));
  Hex_Digit_Display hex_digit_display_5 (.value(DSR));  // open: dp
  Clock clock_1 (.out(clock_1_out));
  LED led_1 (.in(comp_1_led));
  LED led_2 (.in(alterador_1_hr));
  Hex_Digit_Display hex_digit_display_6 (.value(DH));  // open: dp
  Hex_Digit_Display hex_digit_display_7 (.value(USR));  // open: dp
  Hex_Digit_Display hex_digit_display_8 (.value(UH));  // open: dp
  teste teste_1 (
    .min_dez(DMR), .hr_dez(DHR), .hr_uni(UHR), .rst(RST), .min_uni(UMR), .seg_dez(DSR), .seg_uni(USR),
    .HORA_R(HORA_R), .ON_OFF(in_4), .MIN_R(MIN_R), .SEG_R(out_7), .CLK(clock_1_out));
  Button button_3 (.out(RST));
  LED led_3 (.in(alterador_1_min));
  Hex_Digit_Display hex_digit_display_9 (.value(DM));  // open: dp
  Hex_Digit_Display hex_digit_display_10 (.value(UM));  // open: dp
  Demultiplexer #(.select(2), .enable("false")) demultiplexer_2 (
    .out0(out_8), .out1(MIN_A), .out2(HORA_A), .out3(demultiplexer_2_out3), .in(button_4_out), .sel(out_9));
  Button button_4 (.out(button_4_out));
  LED led_4 (.in(alterador_1_seg));
  Hex_Digit_Display hex_digit_display_11 (.value(DS));  // open: dp
  Hex_Digit_Display hex_digit_display_12 (.value(US));  // open: dp
  Hex_Digit_Display hex_digit_display_13 (.value(UHA));  // open: dp
  Hex_Digit_Display hex_digit_display_14 (.value(DHA));  // open: dp
  Hex_Digit_Display hex_digit_display_15 (.value(DMA));  // open: dp
  teste teste_2 (
    .min_dez(DMA), .hr_dez(DHA), .hr_uni(UHA), .rst(RST_A), .min_uni(UMA), .seg_dez(DSA), .seg_uni(USA),
    .HORA_R(HORA_A), .ON_OFF(in_5), .MIN_R(MIN_A), .SEG_R(out_8), .CLK(in_3));
  Hex_Digit_Display hex_digit_display_16 (.value(UMA));  // open: dp
  Button button_5 (.out(RST_A));
  Hex_Digit_Display hex_digit_display_17 (.value(USA));  // open: dp
  Hex_Digit_Display hex_digit_display_18 (.value(DSA));  // open: dp
  Button button_6 ();  // open: out
  Button button_7 ();  // open: out
  Button button_8 ();  // open: out
  Button button_9 ();  // open: out
  Button button_10 ();  // open: out
  Button button_11 ();  // open: out
  multiplex multiplex_1 (
    .DH(DH), .UH(UH), .DM(DM), .UM(UM), .DS(DS), .US(US), .ON_OFF(in_1), .CHANGE(in_2), .DHR(DHR), .DHA(DHA),
    .UHR(UHR), .UHA(UHA), .DMR(DMR), .DMA(DMA), .UMR(UMR), .UMA(UMA), .DSR(DSR), .DSA(DSA), .USR(USR),
    .USA(USA));

  // Other names for the same wires on the sheet: CLK = in_3; ON_OFF = in_5; SEG_A = out_8; SEG_R = out_7
endmodule

module cont_09 (
  input  clk,
  input  rst,
  output [3:0] display,
  output next
);

  wire or_1_out;
  wire [3:0] adder_1_out;

  Hex_Digit_Display hex_digit_display_1 (.value(display));  // open: dp
  Register #(.width(4)) register_1 (.D(adder_1_out), .Q(display), .clk(clk), .clr(or_1_out));  // open: en
  or or_1 (or_1_out, next, rst);
  Adder #(.width(4)) adder_1 (.a(display), .b(4'b0001), .out(adder_1_out));  // open: cin, cout
  and and_1 (next, display[3], ~display[2], display[1], ~display[0]);  // AND_Gate
endmodule

module cont_059 (
  input  clk_seg,
  input  reset,
  output [3:0] dezena,
  output [3:0] unidade,
  output next
);

  wire cont_09_2_next, or_1_out;

  and and_1 (next, ~dezena[0], dezena[1], dezena[2], ~dezena[3]);  // AND_Gate
  or or_1 (or_1_out, next, reset);
  Hex_Digit_Display hex_digit_display_1 (.value(dezena));  // open: dp
  cont_09 cont_09_1 (.display(dezena), .clk(cont_09_2_next), .rst(or_1_out));  // open: next
  Hex_Digit_Display hex_digit_display_2 (.value(unidade));  // open: dp
  cont_09 cont_09_2 (.display(unidade), .clk(clk_seg), .rst(or_1_out), .next(cont_09_2_next));
endmodule

module cont_min (
  input  clk_min,
  input  reset,
  output [3:0] dezena,
  output [3:0] unidade,
  output next
);

  wire cont_09_2_next, or_1_out;
  wire [3:0] undriven, undriven_2;

  and and_1 (next, ~dezena[0], dezena[1], dezena[2], ~dezena[3]);  // AND_Gate
  or or_1 (or_1_out, next, reset);
  Hex_Digit_Display hex_digit_display_1 (.value(dezena));  // open: dp
  cont_09 cont_09_1 (.display(dezena), .clk(cont_09_2_next), .rst(or_1_out));  // open: next
  Hex_Digit_Display hex_digit_display_2 (.value(unidade));  // open: dp
  cont_09 cont_09_2 (.display(unidade), .clk(clk_min), .rst(or_1_out), .next(cont_09_2_next));
  Hex_Digit_Display hex_digit_display_3 (.value(undriven));  // open: dp
  Hex_Digit_Display hex_digit_display_4 (.value(undriven_2));  // open: dp
endmodule

module cont_hr (
  input  clk_hr,
  input  reset_hr,
  output [3:0] dez_hr,
  output [3:0] uni_hr
);

  wire and_1_out, and_2_out, and_3_out, cont_09_2_next, or_1_out;

  and and_1 (and_1_out, ~dez_hr[0], dez_hr[1], ~dez_hr[2], ~dez_hr[3]);  // AND_Gate
  Hex_Digit_Display hex_digit_display_1 (.value(dez_hr));  // open: dp
  Hex_Digit_Display hex_digit_display_2 (.value(uni_hr));  // open: dp
  cont_09 cont_09_1 (.display(dez_hr), .clk(cont_09_2_next), .rst(or_1_out));  // open: next
  or or_1 (or_1_out, reset_hr, and_2_out);
  and and_2 (and_2_out, and_1_out, and_3_out);
  cont_09 cont_09_2 (.display(uni_hr), .clk(clk_hr), .rst(or_1_out), .next(cont_09_2_next));
  and and_3 (and_3_out, ~uni_hr[3], uni_hr[2], ~uni_hr[1], ~uni_hr[0]);  // AND_Gate
endmodule

module teste (
  input  CLK,
  input  HORA_R,
  input  MIN_R,
  input  ON_OFF,
  input  SEG_R,
  input  rst,
  output [3:0] min_dez,
  output [3:0] seg_dez,
  output [3:0] seg_uni,
  output [3:0] hr_dez,
  output [3:0] hr_uni,
  output [3:0] min_uni
);

  wire and_1_out, cont_059_1_next, cont_min_1_next, or_1_out, or_2_out, or_3_out;

  Hex_Digit_Display hex_digit_display_1 (.value(hr_dez));  // open: dp
  cont_hr cont_hr_1 (.dez_hr(hr_dez), .reset_hr(rst), .uni_hr(hr_uni), .clk_hr(or_1_out));
  Hex_Digit_Display hex_digit_display_2 (.value(hr_uni));  // open: dp
  or or_1 (or_1_out, cont_min_1_next, HORA_R);
  Hex_Digit_Display hex_digit_display_3 (.value(min_dez));  // open: dp
  Hex_Digit_Display hex_digit_display_4 (.value(min_uni));  // open: dp
  cont_min cont_min_1 (.dezena(min_dez), .unidade(min_uni), .next(cont_min_1_next), .reset(rst), .clk_min(or_2_out));
  or or_2 (or_2_out, cont_059_1_next, MIN_R);
  Hex_Digit_Display hex_digit_display_5 (.value(seg_dez));  // open: dp
  Hex_Digit_Display hex_digit_display_6 (.value(seg_uni));  // open: dp
  cont_059 cont_059_1 (.dezena(seg_dez), .next(cont_059_1_next), .reset(rst), .unidade(seg_uni), .clk_seg(or_3_out));
  or or_3 (or_3_out, and_1_out, SEG_R);
  and and_1 (and_1_out, CLK, ON_OFF);
endmodule

module comp (
  input  [3:0] UNID_SEG_HR,
  input  [3:0] UNID_SEG_AL,
  input  [3:0] DEZ_SEG_HR,
  input  [3:0] DEZ_SEG_AL,
  input  [3:0] UNID_MIN_HR,
  input  [3:0] UNID_MIN_AL,
  input  [3:0] DEZ_MIN_HR,
  input  [3:0] DEZ_MIN_AL,
  input  [3:0] UNID_HR_R,
  input  [3:0] UNID_HR_AL,
  input  [3:0] DEZ_HR_R,
  input  [3:0] UNID_HR_AL_2,
  output LED
);

  wire comparator_1_eq, comparator_3_eq, comparator_4_eq, comparator_5_eq, comparator_6_eq;

  Comparator #(.width(4)) comparator_1 (.a(UNID_SEG_HR), .b(UNID_SEG_AL), .eq(comparator_1_eq));  // open: gt, lt
  Comparator #(.width(4)) comparator_2 (.a(DEZ_SEG_HR), .b(DEZ_SEG_AL), .eq(comparator_1_eq));  // open: gt, lt
  Comparator #(.width(4)) comparator_3 (.a(UNID_MIN_HR), .b(UNID_MIN_AL), .eq(comparator_3_eq));  // open: gt, lt
  Comparator #(.width(4)) comparator_4 (.a(DEZ_MIN_HR), .b(DEZ_MIN_AL), .eq(comparator_4_eq));  // open: gt, lt
  Comparator #(.width(4)) comparator_5 (.a(UNID_HR_R), .b(UNID_HR_AL), .eq(comparator_5_eq));  // open: gt, lt
  Comparator #(.width(4)) comparator_6 (.a(DEZ_HR_R), .b(UNID_HR_AL_2), .eq(comparator_6_eq));  // open: gt, lt
  and and_1 (LED, comparator_1_eq, comparator_1_eq, comparator_3_eq, comparator_4_eq, comparator_5_eq, comparator_6_eq);
endmodule

module multiplex (
  input  ON_OFF,
  input  CHANGE,
  input  [3:0] DHR,
  input  [3:0] DHA,
  input  [3:0] UHR,
  input  [3:0] UHA,
  input  [3:0] DMR,
  input  [3:0] DMA,
  input  [3:0] UMR,
  input  [3:0] UMA,
  input  [3:0] DSR,
  input  [3:0] DSA,
  input  [3:0] USR,
  input  [3:0] USA,
  output [3:0] DH,
  output [3:0] UH,
  output [3:0] DM,
  output [3:0] UM,
  output [3:0] DS,
  output [3:0] US
);

  wire button_1_out, undriven, undriven_2, undriven_3;
  wire [1:0] counter_1_q;

  Multiplexer #(.width(4)) multiplexer_1 (.in0(DHR), .in1(DHA), .out(DH), .sel(CHANGE), .en(ON_OFF));
  Multiplexer #(.width(4)) multiplexer_2 (.in0(UHR), .in1(UHA), .out(UH), .sel(CHANGE), .en(ON_OFF));
  Multiplexer #(.width(4)) multiplexer_3 (.in0(DMR), .in1(DMA), .out(DM), .sel(CHANGE), .en(ON_OFF));
  Counter #(.width(2), .max('h3)) counter_1 (.Q(counter_1_q), .clk(button_1_out));  // open: load, D, count, carry, clr
  Button button_1 (.out(button_1_out));
  Multiplexer #(.width(4)) multiplexer_4 (.in0(UMR), .in1(UMA), .out(UM), .sel(CHANGE), .en(ON_OFF));
  Multiplexer #(.width(4)) multiplexer_5 (.in0(DSR), .in1(DSA), .out(DS), .sel(CHANGE), .en(ON_OFF));
  Multiplexer #(.width(4)) multiplexer_6 (.in0(USR), .in1(USA), .out(US), .sel(CHANGE), .en(ON_OFF));
  Multiplexer #(.select(2), .enable("false")) multiplexer_7 (
    .in0(undriven), .in2(undriven_2), .in3(undriven_3), .sel(counter_1_q));  // open: in1, out

  // Other names for the same wires on the sheet: Al_Rel = CHANGE; LIGAR = ON_OFF
endmodule

module ALTERADOR (
  input  ENTRADA,
  output [1:0] MS,
  output MIN,
  output SEG,
  output HR
);

  wire and_1_out, and_2_out, nor_1_out;
  wire [1:0] adder_1_out;

  Counter #(.width(2), .max('h3)) counter_1 (
    .D(adder_1_out), .Q({HR, MIN}), .clk(ENTRADA));  // open: load, count, carry, clr
  Adder #(.width(2)) adder_1 (.a({HR, MIN}), .b(2'b11), .out(adder_1_out));  // open: cin, cout
  LED led_1 (.in(MIN));
  LED led_2 (.in(HR));
  and and_1 (and_1_out, MIN, HR);
  nor nor_1 (nor_1_out, MIN, HR);
  LED led_3 (.in(SEG));
  or or_1 (SEG, and_1_out, nor_1_out);
  and and_2 (and_2_out, SEG, MIN, HR);
  LED led_4 (.in(and_2_out));

  assign MS = {HR, MIN};

  // Other names for the same wires on the sheet: M = MIN; H = HR; S = SEG
endmodule

module demu (
  input  in_1,
  input  PAUSE_minus,
  input  in_3,
  input  in_4,
  output out_5,
  output out_6,
  output [1:0] out_7,
  output [1:0] out_8
);

  wire A, ALTER_minus_out, alterador_1_hr, alterador_1_min, alterador_1_seg, B, CLK, clock_1_out, comp_1_led,
       demultiplexer_1_out3, demultiplexer_2_out3, demultiplexer_3_out2, HORA_A, HORA_R, MIN_A, MIN_R,
       MODE_minus_out, nor_1_out, RST, RST_A, SELECT_minus_out;
  wire [3:0] DH, DHA, DHR, DM, DMA, DMR, DS, DSA, DSR, UH, UHA, UHR, UM, UMA, UMR, US, USA, USR;

  Hex_Digit_Display hex_digit_display_1 (.value(DHR));  // open: dp
  Button SELECT_minus (.out(SELECT_minus_out));
  Hex_Digit_Display hex_digit_display_2 (.value(UHR));  // open: dp
  ALTERADOR alterador_1 (
    .MS(out_7), .MIN(alterador_1_min), .ENTRADA(SELECT_minus_out), .HR(alterador_1_hr), .SEG(alterador_1_seg));
  Demultiplexer #(.select(2), .enable("false")) demultiplexer_1 (
    .out0(out_5), .out1(MIN_R), .out2(HORA_R), .out3(demultiplexer_1_out3), .in(A), .sel(out_7));
  Hex_Digit_Display hex_digit_display_3 (.value(DMR));  // open: dp
  Hex_Digit_Display hex_digit_display_4 (.value(UMR));  // open: dp
  comp comp_1 (
    .UNID_SEG_HR(USR), .UNID_SEG_AL(USA), .DEZ_SEG_HR(DSR), .DEZ_SEG_AL(DSA), .UNID_MIN_HR(UMR),
    .UNID_MIN_AL(UMA), .DEZ_MIN_HR(DMR), .DEZ_MIN_AL(DMA), .UNID_HR_R(UHR), .UNID_HR_AL(UHA), .DEZ_HR_R(DHR),
    .UNID_HR_AL_2(DHA), .LED(comp_1_led));
  Hex_Digit_Display hex_digit_display_5 (.value(DSR));  // open: dp
  Clock clock_1 (.out(clock_1_out));
  LED led_1 (.in(comp_1_led));
  LED led_2 (.in(alterador_1_hr));
  Hex_Digit_Display hex_digit_display_6 (.value(DH));  // open: dp
  Hex_Digit_Display hex_digit_display_7 (.value(USR));  // open: dp
  Hex_Digit_Display hex_digit_display_8 (.value(UH));  // open: dp
  teste teste_1 (
    .min_dez(DMR), .hr_dez(DHR), .hr_uni(UHR), .rst(RST), .min_uni(UMR), .seg_dez(DSR), .seg_uni(USR),
    .HORA_R(HORA_R), .ON_OFF(PAUSE_minus), .MIN_R(MIN_R), .SEG_R(out_5), .CLK(clock_1_out));
  Button button_1 (.out(RST));
  LED led_3 (.in(alterador_1_min));
  Hex_Digit_Display hex_digit_display_9 (.value(DM));  // open: dp
  Hex_Digit_Display hex_digit_display_10 (.value(UM));  // open: dp
  Demultiplexer #(.select(2), .enable("false")) demultiplexer_2 (
    .out0(out_6), .out1(MIN_A), .out2(HORA_A), .out3(demultiplexer_2_out3), .in(B), .sel(out_7));
  LED led_4 (.in(alterador_1_seg));
  Hex_Digit_Display hex_digit_display_11 (.value(DS));  // open: dp
  Hex_Digit_Display hex_digit_display_12 (.value(US));  // open: dp
  Button MODE_minus (.out(MODE_minus_out));
  Hex_Digit_Display hex_digit_display_13 (.value(DHA));  // open: dp
  Hex_Digit_Display hex_digit_display_14 (.value(UHA));  // open: dp
  Counter #(.width(2), .max('h2)) counter_1 (.Q(out_8), .clk(MODE_minus_out));  // open: load, D, count, carry, clr
  Hex_Digit_Display hex_digit_display_15 (.value(DMA));  // open: dp
  teste teste_2 (
    .min_dez(DMA), .hr_dez(DHA), .hr_uni(UHA), .rst(RST_A), .min_uni(UMA), .seg_dez(DSA), .seg_uni(USA),
    .HORA_R(HORA_A), .ON_OFF(in_3), .MIN_R(MIN_A), .SEG_R(out_6), .CLK(CLK));
  Demultiplexer #(.select(2), .enable("false")) demultiplexer_3 (
    .out0(A), .out1(B), .out2(demultiplexer_3_out2), .in(ALTER_minus_out), .sel(out_8));  // open: out3
  Button ALTER_minus (.out(ALTER_minus_out));
  Hex_Digit_Display hex_digit_display_16 (.value(UMA));  // open: dp
  Button button_2 (.out(RST_A));
  Hex_Digit_Display hex_digit_display_17 (.value(DSA));  // open: dp
  Hex_Digit_Display hex_digit_display_18 (.value(USA));  // open: dp
  Button button_3 ();  // open: out
  Button button_4 ();  // open: out
  Button button_5 ();  // open: out
  Button button_6 ();  // open: out
  Button button_7 ();  // open: out
  Button button_8 ();  // open: out
  multiplex multiplex_1 (
    .DH(DH), .UH(UH), .DM(DM), .UM(UM), .DS(DS), .US(US), .ON_OFF(in_1), .CHANGE(out_8[0]), .DHR(DHR),
    .DHA(DHA), .UHR(UHR), .UHA(UHA), .DMR(DMR), .DMA(DMA), .UMR(UMR), .UMA(UMA), .DSR(DSR), .DSA(DSA),
    .USR(USR), .USA(USA));
  LED led_5 (.in(out_8[0]));
  LED led_6 (.in(out_8[1]));
  nor nor_1 (nor_1_out, out_8[1], out_8[0]);
  LED led_7 (.in(nor_1_out));

  // Other names for the same wires on the sheet: ON_OFF = in_3; S[1:0] = out_8; SEG_A = out_6; SEG_R = out_5
endmodule
